# Fritzing sketch Untitled Sketch 2 (saved by Fritzing 0.9.9b)
breadboards: 1

parts:
  M1 = STM32F103C8T6 blue mini board
  Parça1 = Bluetooth HC-05 Macho
  VCC1 = Battery block 9V
  LCM1602_IIC1 = LCM1602 IIC [part_number="LCM1602 IIC" chip_label="LCM1602 IIC" package="DIP (Dual Inline) [THT]"]
  U1 = LCD-16X2 [package=lcd-16x2]
  1 = Basic Servo
  4 = Basic Servo
  2 = Basic Servo
  5 = Basic Servo
  3 = Basic Servo

nets:
  N1: M1.A8, 1.pulse
  N2: M1.A9, Parça1.RXD
  N3: M1.A10, Parça1.TXD
  N4: M1.B6, LCM1602_IIC1.SCL
  N5: M1.B7, LCM1602_IIC1.SDA
  5V: M1.5V, LCM1602_IIC1.VCC
  GND: M1.G, Parça1.GND, VCC1.-, LCM1602_IIC1.GND, 1.gnd, 4.gnd, 2.gnd, 5.gnd, 3.gnd
  3.3V: M1.3.3V, M1.3.3, Parça1.VCC
  N6: M1.A0, 2.pulse
  N7: M1.A1, 3.pulse
  N8: M1.A2, 4.pulse
  N9: M1.A3, 5.pulse
  VCC: VCC1.+, 1.vcc, 4.vcc, 2.vcc, 5.vcc, 3.vcc
  VSS: LCM1602_IIC1.VSS, U1.VSS
  VDD: LCM1602_IIC1.VDD, U1.VDD
  N10: LCM1602_IIC1.V0, U1.VO
  N11: LCM1602_IIC1.RS, U1.RS
  N12: LCM1602_IIC1.RW, U1.R_W
  N13: LCM1602_IIC1.E, U1.E
  N14: LCM1602_IIC1.D0, U1.DB0
  N15: LCM1602_IIC1.D1, U1.DB1
  N16: LCM1602_IIC1.D2, U1.DB2
  N17: LCM1602_IIC1.D3, U1.DB3
  N18: LCM1602_IIC1.D4, U1.DB4
  N19: LCM1602_IIC1.D5, U1.DB5
  N20: LCM1602_IIC1.D6, U1.DB6
  N21: LCM1602_IIC1.D7, U1.DB7
  N22: LCM1602_IIC1.A, U1.A
  N23: LCM1602_IIC1.K, U1.K
  N24: LCM1602_IIC1.LED_A, LCM1602_IIC1.LED_B

custom parts:
  LCM1602 IIC: I2C-Module to use a 1602 or 2004 LCD on with the wire.h libory Serial LCD Modul
